// Logisim project Latches.circ as structural Verilog: 1 circuit, main circuit main
module main (
  input  R,
  input  R_2,
  input  S,
  input  S_2,
  input  K,
  input  J,
  input  K_2,
  input  J_2,
  input  S_3,
  input  S_4,
  input  R_3,
  input  R_4,
  input  D,
  input  D_2,
  input  D_3,
  input  D_4,
  output Q,
  output Q_2,
  output nQ,
  output nQ_2,
  output Q_3,
  output Q_4,
  output nQ_3,
  output nQ_4,
  output Q_5,
  output Q_6,
  output nQ_5,
  output nQ_6,
  output Q_7,
  output Q_8,
  output nQ_7,
  output nQ_8,
  output Q_9,
  output nQ_9,
  output Q_10,
  output nQ_10
);

  wire and_1_out, and_2_out, and_3_out, and_4_out, and_5_out, and_6_out, clock_1_out, clock_2_out,
       clock_3_out, clock_4_out, clock_5_out, clock_6_out, nand_5_out, nand_6_out, nand_7_out, nand_8_out,
       nand_9_out, nand_10_out, nand_11_out, nand_12_out, nand_13_out, nand_14_out, nand_19_out, nand_20_out,
       nand_21_out, nand_22_out, not_1_out, not_2_out, not_3_out, not_4_out;

  Clock clock_1 (.out(clock_1_out));
  Clock clock_2 (.out(clock_2_out));
  not not_1 (not_1_out, D);
  not not_2 (not_2_out, clock_1_out);
  nor nor_1 (Q, R, nQ);
  nor nor_2 (nQ, Q, S);
  and and_1 (and_1_out, Q_3, J);
  and and_2 (and_2_out, K_2, nQ_3);
  nand nand_1 (Q_5, S_3, nQ_5);
  nand nand_2 (nQ_5, Q_5, R_3);
  nand nand_3 (Q_7, D, nQ_7);
  nand nand_4 (nQ_7, Q_7, not_1_out);
  nand nand_5 (nand_5_out, D_3, not_2_out);
  nand nand_6 (nand_6_out, nand_5_out, not_2_out);
  nor nor_3 (Q_3, and_1_out, nQ_3);
  nor nor_4 (nQ_3, Q_3, and_2_out);
  not not_3 (not_3_out, not_2_out);
  nand nand_7 (nand_7_out, nand_10_out, nand_8_out);
  nand nand_8 (nand_8_out, nand_7_out, clock_2_out);
  nand nand_9 (nand_9_out, nand_8_out, clock_2_out, nand_10_out);
  nand nand_10 (nand_10_out, nand_9_out, D_4);
  Clock clock_3 (.out(clock_3_out));
  Clock clock_4 (.out(clock_4_out));
  Clock clock_5 (.out(clock_5_out));
  nand nand_11 (nand_11_out, nand_5_out, nand_12_out);
  nand nand_12 (nand_12_out, nand_11_out, nand_6_out);
  and and_3 (and_3_out, R_2, clock_3_out);
  and and_4 (and_4_out, clock_3_out, S_2);
  Clock clock_6 (.out(clock_6_out));
  nand nand_13 (nand_13_out, S_4, clock_4_out);
  nand nand_14 (nand_14_out, clock_4_out, R_4);
  not not_4 (not_4_out, D_2);
  nand nand_15 (Q_10, nand_8_out, nQ_10);
  nand nand_16 (nQ_10, Q_10, nand_9_out);
  nor nor_5 (Q_2, and_3_out, nQ_2);
  nor nor_6 (nQ_2, Q_2, and_4_out);
  and and_5 (and_5_out, Q_4, K, clock_6_out);
  and and_6 (and_6_out, clock_6_out, J_2, nQ_4);
  nand nand_17 (Q_6, nand_13_out, nQ_6);
  nand nand_18 (nQ_6, Q_6, nand_14_out);
  nand nand_19 (nand_19_out, D_2, clock_5_out);
  nand nand_20 (nand_20_out, clock_5_out, not_4_out);
  nand nand_21 (nand_21_out, nand_11_out, not_3_out);
  nand nand_22 (nand_22_out, nand_21_out, not_3_out);
  nor nor_7 (nQ_4, Q_4, and_6_out);
  nand nand_23 (Q_8, nand_19_out, nQ_8);
  nand nand_24 (nQ_8, Q_8, nand_20_out);
  nand nand_25 (Q_9, nand_21_out, nQ_9);
  nand nand_26 (nQ_9, Q_9, nand_22_out);
  Button button_1 (.out(Q_4));
  nor nor_8 (Q_4, and_5_out, nQ_4);

  // Notes on the sheet:
  //   S-R NOR Latch
  //   S-R NAND Latch
  //    D NAND Latch
  //   Positive edge D flip-flop
  //   J-K Latch
  //   Positive Edge Triggered Master-Slave D Flip Flop
  //   Clocked S-R Latch
  //   Clocked J-K Latch
  //   Clocked S-R Latch
  //   Clocked NAND D Latch
endmodule
