// Logisim project sec.circ as structural Verilog: 1 circuit, main circuit main
module main (
);

  wire A0, A1, A2, C0, C0e, C1, C1e, C2, C2e, C3, C3e, clock_1_out, D0, D0e, D1, D1e, D2, D2e, D3, D3e, D4,
       D4e, D5, D5e, D6, D6e, D7, D7e, fromc0, fromc1, fromc2, fromc3, go, multiplexer_2_out,
       multiplexer_3_out, multiplexer_4_out, multiplexer_5_out, multiplexer_6_out, multiplexer_8_out,
       multiplexer_9_out, multiplexer_10_out, not_1_out, not_2_out, not_5_out, not_6_out, not_9_out,
       not_10_out, not_12_out, not_13_out, not_16_out, not_17_out, not_19_out, not_20_out, P0, P1, P2,
       Reset_out, t_ff_1_q, t_ff_2_q, t_ff_3_q, t_ff_4_q, t_ff_5_q, t_ff_6_q, xor_5_out, xor_6_out,
       xor_7_out, xor_8_out, xor_9_out, xor_10_out, xor_11_out, xor_12_out, xor_13_out, xor_14_out, Z0, Z1,
       Z2, Z3, Z4, Z5, Z6, Z7;
  wire [0:0] multiplexer_1_out;
  wire [3:0] xor_1_out;

  Clock clock_1 (.out(clock_1_out));
  T_Flip_Flop t_ff_1 (.clk(clock_1_out), .T(1'b1), .Q(t_ff_1_q), .Qn(P0), .preset(Reset_out), .en(go));  // open: reset
  Multiplexer #(.select(3), .disabled(0), .enable("false")) multiplexer_1 (
    .in0(Z7), .in1(Z6), .in2(Z5), .in3(Z4), .in4(Z3), .in5(Z2), .in6(Z1), .in7(Z0),
    .out(multiplexer_1_out[0]), .sel({P2, P1, P0}));
  T_Flip_Flop t_ff_2 (.clk(t_ff_1_q), .T(1'b1), .Q(t_ff_2_q), .Qn(P1), .preset(Reset_out));  // open: reset, en
  T_Flip_Flop t_ff_3 (.clk(t_ff_2_q), .T(1'b1), .Q(t_ff_3_q), .Qn(P2), .preset(Reset_out));  // open: reset, en
  ROM #(.addrWidth(3), .dataWidth(12)) rom_1 (
    .addr({A2, A1, A0}), .data({D7, D6, D5, D4, C3, D3, D2, D1, C2, D0, C1, C0}));  // open: sel
  TTY #(.cols(8)) tty_1 (.data({6'b011000, multiplexer_1_out[0]}), .clk(clock_1_out), .we(go), .clr(Reset_out));
  T_Flip_Flop t_ff_4 (.clk(t_ff_3_q), .T(1'b1), .Q(t_ff_4_q), .Qn(A0), .preset(Reset_out));  // open: reset, en
  // Probe on {D7, D6, D5, D4, C3, D3, D2, D1, C2, D0, C1, C0}
  T_Flip_Flop t_ff_5 (.clk(t_ff_4_q), .T(1'b1), .Q(t_ff_5_q), .Qn(A1), .preset(Reset_out));  // open: reset, en
  T_Flip_Flop t_ff_6 (.clk(t_ff_5_q), .T(1'b1), .Q(t_ff_6_q), .Qn(A2), .preset(Reset_out));  // open: reset, en
  Button Reset (.out(Reset_out));
  T_Flip_Flop t_ff_7 (.clk(t_ff_6_q), .T(1'b1), .Q(go), .preset(Reset_out));  // open: Qn, reset, en
  not not_1 (not_1_out, D6);
  not not_2 (not_2_out, D7);
  Multiplexer multiplexer_2 (.in0(not_1_out), .in1(D6), .out(multiplexer_2_out), .sel(D6e));  // open: en
  Multiplexer multiplexer_3 (.in0(not_2_out), .in1(D7), .out(multiplexer_3_out), .sel(D7e));  // open: en
  not not_3 (Z6, multiplexer_2_out);
  not not_4 (Z7, multiplexer_3_out);
  not not_5 (not_5_out, D5);
  not not_6 (not_6_out, D4);
  Multiplexer multiplexer_4 (.in0(not_6_out), .in1(D4), .out(multiplexer_4_out), .sel(D4e));  // open: en
  Multiplexer multiplexer_5 (.in0(not_5_out), .in1(D5), .out(multiplexer_5_out), .sel(D5e));  // open: en
  not not_7 (Z5, multiplexer_5_out);
  not not_8 (Z4, multiplexer_4_out);
  not not_9 (not_9_out, D3);
  not not_10 (not_10_out, C3);
  Multiplexer multiplexer_6 (.in0(not_9_out), .in1(D3), .out(multiplexer_6_out), .sel(D3e));  // open: en
  Multiplexer multiplexer_7 (.in0(not_10_out), .in1(C3), .sel(C3e));  // open: out, en
  not not_11 (Z3, multiplexer_6_out);
  not not_12 (not_12_out, D2);
  not not_13 (not_13_out, D1);
  Multiplexer multiplexer_8 (.in0(not_12_out), .in1(D2), .out(multiplexer_8_out), .sel(D2e));  // open: en
  Multiplexer multiplexer_9 (.in0(not_13_out), .in1(D1), .out(multiplexer_9_out), .sel(D1e));  // open: en
  not not_14 (Z1, multiplexer_9_out);
  not not_15 (Z2, multiplexer_8_out);
  not not_16 (not_16_out, C2);
  not not_17 (not_17_out, D0);
  Multiplexer multiplexer_10 (.in0(not_17_out), .in1(D0), .out(multiplexer_10_out), .sel(D0e));  // open: en
  Multiplexer multiplexer_11 (.in0(not_16_out), .in1(C2), .sel(C2e));  // open: out, en
  not not_18 (Z0, multiplexer_10_out);
  not not_19 (not_19_out, C1);
  not not_20 (not_20_out, C0);
  Multiplexer multiplexer_12 (.in0(not_19_out), .in1(C1), .sel(C1e));  // open: out, en
  Multiplexer multiplexer_13 (.in0(not_20_out), .in1(C0), .sel(C0e));  // open: out, en
  xor xor_1 (xor_1_out[0], C0, fromc0);
  xor xor_2 (xor_1_out[1], C1, fromc1);
  xor xor_3 (xor_1_out[2], C2, fromc2);
  xor xor_4 (xor_1_out[3], C3, fromc3);
  xor xor_5 (xor_5_out, D0, D1);
  xor xor_6 (xor_6_out, D3, D4);
  xor xor_7 (xor_7_out, D0, D2);
  xor xor_8 (xor_8_out, D3, D5);
  xor xor_9 (xor_9_out, D1, D2);
  xor xor_10 (xor_10_out, D3, D6);
  xor xor_11 (xor_11_out, D4, D5);
  xor xor_12 (xor_12_out, D6, D7);
  Decoder #(.select(4)) decoder_1 (
    .out0(C0e), .out1(C1e), .out2(D0e), .out3(C2e), .out4(D1e), .out5(D2e), .out6(D3e), .out7(C3e),
    .out8(D4e), .out9(D5e), .out10(D6e), .out11(D7e), .sel(xor_1_out));  // open: out12, out13, out14, out15, en
  // Probe on xor_1_out
  xor xor_13 (xor_13_out, xor_5_out, xor_6_out);
  xor xor_14 (xor_14_out, xor_7_out, xor_8_out);
  xor xor_15 (fromc2, xor_9_out, xor_10_out);
  xor xor_16 (fromc3, xor_11_out, xor_12_out);
  xor xor_17 (fromc0, xor_13_out, D6);
  xor xor_18 (fromc1, xor_14_out, D6);

  // Other names for the same wires on the sheet: goc0[4:0] = {D6, D4, D3, D1, D0}; goc1[4:0] = {D6, D5, D3, D2, D0};
  //   goc2[3:0] = {D6, D3, D2, D1}; goc3[3:0] = {D7, D6, D5, D4}

  // Notes on the sheet:
  //   Wai Shing Yung
  //   996936848
  //   Wai Shing Yung
  //   996936848
  //   contents of rom_1 (hex, n*v repeats v):
  //   d7 788 a75 a74 275 b75 f75 a77
  //   00101011
  //   01110000
  //   10101111
  //   10101111
  //   10101111
  //   10101111
  //   11111111
  //   10101111
  //   anti-claustrophobia
endmodule
