// Logisim project updown.circ as structural Verilog: 1 circuit, main circuit main
module main (
);

  wire and_1_out, clock_1_out, clock_2_out, clock_3_out, d_ff_1_qn, d_ff_2_qn, d_ff_3_qn, d_ff_4_qn,
       d_ff_5_qn, d_ff_6_qn, not_1_out, Q0, Q1, Q2, Reset_out, stop, Up_Down;
  wire [2:0] d_ff_1_q, d_ff_3_q;

  Clock clock_1 (.out(clock_1_out));
  D_Flip_Flop d_ff_1 (.clk(clock_1_out), .D(d_ff_1_qn), .Q(d_ff_1_q[0]), .Qn(d_ff_1_qn));  // open: preset, en, reset
  Clock clock_2 (.out(clock_2_out));
  D_Flip_Flop d_ff_2 (.clk(d_ff_1_qn), .D(d_ff_2_qn), .Q(d_ff_1_q[1]), .Qn(d_ff_2_qn));  // open: preset, en, reset
  D_Flip_Flop d_ff_3 (.clk(clock_2_out), .D(d_ff_3_qn), .Q(d_ff_3_q[0]), .Qn(d_ff_3_qn));  // open: preset, en, reset
  D_Flip_Flop d_ff_4 (.clk(d_ff_2_qn), .D(d_ff_4_qn), .Q(d_ff_1_q[2]), .Qn(d_ff_4_qn));  // open: preset, en, reset
  D_Flip_Flop d_ff_5 (.clk(d_ff_3_q[0]), .D(d_ff_5_qn), .Q(d_ff_3_q[1]), .Qn(d_ff_5_qn));  // open: preset, en, reset
  D_Flip_Flop d_ff_6 (.clk(d_ff_3_q[1]), .D(d_ff_6_qn), .Q(d_ff_3_q[2]), .Qn(d_ff_6_qn));  // open: preset, en, reset
  Multiplexer #(.width(3)) multiplexer_1 (
    .in0(d_ff_1_q), .in1(d_ff_3_q), .out({Q2, Q1, Q0}), .sel(Up_Down));  // open: en
  Clock clock_3 (.out(clock_3_out));
  not not_1 (not_1_out, stop);
  and and_1 (and_1_out, clock_3_out, not_1_out);
  TTY #(.rows(1), .cols(21)) tty_1 (.data({4'b0110, Q2, Q1, Q0}), .clk(and_1_out), .clr(Reset_out));  // open: we
  Counter #(.width(5), .max('h14), .ongoal("stay")) counter_1 (
    .carry(stop), .clk(and_1_out), .clr(Reset_out));  // open: load, D, count, Q
  Counter #(.width(5), .max('h9), .ongoal("stay")) counter_2 (
    .carry(Up_Down), .clk(and_1_out), .clr(Reset_out));  // open: load, D, count, Q
  Button Reset (.out(Reset_out));

  // Notes on the sheet:
  //   Wai Shing Yung
  //   996936848
  //   70123456776543210765
endmodule
