// Logisim project updowntest.circ as structural Verilog: 1 circuit, main circuit main
module main (
);

  wire and_1_out, clock_1_out, not_1_out, Q0, Q1, Q2, Reset_out, stop, Up_Down;

  Clock clock_1 (.out(clock_1_out));
  not not_1 (not_1_out, stop);
  and and_1 (and_1_out, clock_1_out, not_1_out);
  TTY #(.rows(1), .cols(21)) tty_1 (.data({4'b0110, Q2, Q1, Q0}), .clk(and_1_out), .clr(Reset_out));  // open: we
  Counter #(.width(5), .max('h14), .ongoal("stay")) counter_1 (
    .carry(stop), .clk(and_1_out), .clr(Reset_out));  // open: load, D, count, Q
  Counter #(.width(5), .max('h9), .ongoal("stay")) counter_2 (
    .carry(Up_Down), .clk(and_1_out), .clr(Reset_out));  // open: load, D, count, Q
  Button Reset (.out(Reset_out));

  // Notes on the sheet:
  //   70123456776543210765
endmodule
