// Logisim project four.circ as structural Verilog: 1 circuit, main circuit main
module main (
);

  wire _4_Counter_carry, A_q, A_qn, aBcX_out, AC_out, aCx_out, B_q, B_qn, Bc_out, BCx_2_out, bcx_out, bX_out,
       C_q, C_qn, CLK, clock_1_out, clock_2_out, go, not_1_out, or_1_out, or_2_out, or_3_out, Q, Reset_out, w;
  wire [1:0] _4_Counter_q;
  wire [4:0] _32_Counter_q;

  not not_1 (not_1_out, w);
  and aCx (aCx_out, A_qn, C_q, not_1_out);
  and Bc (Bc_out, B_q, C_qn);
  and bX (bX_out, B_qn, w, w);
  and bcx (bcx_out, B_qn, C_qn, not_1_out);
  and AC (AC_out, A_q, C_q);
  Clock clock_1 (.out(clock_1_out));
  or or_1 (or_1_out, B_q, aCx_out);
  or or_2 (or_2_out, Bc_out, A_q, bX_out);
  or or_3 (or_3_out, AC_out, bcx_out, BCx_2_out, aBcX_out);
  and BCx_2 (BCx_2_out, C_q, B_q, not_1_out);
  and aBcX (aBcX_out, A_qn, B_q, B_qn, w);
  T_Flip_Flop A (.clk(clock_1_out), .T(or_1_out), .Q(A_q), .Qn(A_qn));  // open: preset, reset, en
  T_Flip_Flop B (.clk(clock_1_out), .T(or_2_out), .Q(B_q), .Qn(B_qn));  // open: preset, reset, en
  T_Flip_Flop C (.clk(clock_1_out), .T(or_3_out), .Q(C_q), .Qn(C_qn));  // open: preset, reset, en
  TTY #(.rows(17), .cols(4)) tty_1 (.data({6'b011000, Q}), .clk(CLK), .we(go), .clr(Reset_out));
  Button Reset (.out(Reset_out));
  and and_1 (CLK, clock_2_out, go);
  Clock clock_2 (.out(clock_2_out));
  // Probe on _4_Counter_q
  Counter #(.width(2), .max('h3)) _4_Counter (
    .Q(_4_Counter_q), .carry(_4_Counter_carry), .clk(CLK), .clr(Reset_out));  // open: load, D, count
  and and_2 (Q, A_q, B_q, C_q, w);
  // Probe on _32_Counter_q[3:0]
  Counter #(.width(5), .max('h1f), .trigger("falling")) _32_Counter (
    .Q(_32_Counter_q), .clk(_4_Counter_carry), .clr(Reset_out));  // open: load, D, count, carry
  // Probe on w
  BitSelector #(.width(4)) bitselector_1 (.in(_32_Counter_q[3:0]), .out(w), .sel(_4_Counter_q));
  not not_2 (go, _32_Counter_q[4]);

  // Notes on the sheet:
  //   996936848
  //   Wai Shing Yung
  //   0000
  //   1000
  //   0100
  //   1100
  //   0010
  //   1010
  //   0110
  //   1110
  //   0001
  //   1001
  //   0101
  //   1101
  //   0011
  //   1011
  //   0111
  //   1111
  //   17 gates
  //   0000
  //   0000
  //   0000
  //   0000
  //   0000
  //   0000
  //   0000
  //   0000
  //   0000
  //   0001
  //   0000
  //   0000
  //   0000
  //   0000
  //   0001
  //   0000
endmodule
