// Logisim project parity.circ as structural Verilog: 1 circuit, main circuit main
module main (
);

  wire _4_Counter_carry, CLK, clock_1_out, clock_2_out, d_ff_1_q, d_ff_2_q, d_ff_3_q, go, Out, Reset_out, x,
       xnor_1_out, xnor_2_out;
  wire [1:0] _4_Counter_q;
  wire [3:0] _32_Counter_q_2;
  wire [4:4] _32_Counter_q;

  Clock clock_1 (.out(clock_1_out));
  D_Flip_Flop d_ff_1 (.clk(clock_1_out), .D(x), .Q(d_ff_1_q));  // open: Qn, preset, en, reset
  xnor xnor_1 (xnor_1_out, x, d_ff_1_q);
  D_Flip_Flop d_ff_2 (.clk(clock_1_out), .D(d_ff_1_q), .Q(d_ff_2_q));  // open: Qn, preset, en, reset
  xnor xnor_2 (xnor_2_out, d_ff_2_q, d_ff_3_q);
  D_Flip_Flop d_ff_3 (.clk(clock_1_out), .D(d_ff_2_q), .Q(d_ff_3_q));  // open: Qn, preset, en, reset
  xnor xnor_3 (Out, xnor_2_out, xnor_1_out);
  TTY #(.rows(17), .cols(4)) tty_1 (.data({6'b011000, Out}), .clk(CLK), .we(go), .clr(Reset_out));
  Button Reset (.out(Reset_out));
  Clock clock_2 (.out(clock_2_out));
  // Probe on _4_Counter_q
  Counter #(.width(2), .max('h3)) _4_Counter (
    .Q(_4_Counter_q), .carry(_4_Counter_carry), .clk(CLK), .clr(Reset_out));  // open: load, D, count
  and and_1 (CLK, clock_2_out, go);
  Counter #(.width(5), .max('h1f), .trigger("falling")) _32_Counter (
    .Q({_32_Counter_q[4], _32_Counter_q_2}), .clk(_4_Counter_carry), .clr(Reset_out));  // open: load, D, count, carry
  // Probe on _32_Counter_q_2
  BitSelector #(.width(4)) bitselector_1 (.in(_32_Counter_q_2), .out(x), .sel(_4_Counter_q));
  not not_1 (go, _32_Counter_q[4]);
  // Probe on x

  // Notes on the sheet:
  //   Wai Shing Yung
  //   996936848
  //   22 gates
  //   Input
  //   0000
  //   1000
  //   0100
  //   1100
  //   0010
  //   1010
  //   0110
  //   1110
  //   0001
  //   1001
  //   0101
  //   1101
  //   0011
  //   1011
  //   0111
  //   1111
  //   Key
  //   1111
  //   0000
  //   1000
  //   1111
  //   0100
  //   1111
  //   0111
  //   0000
  //   1010
  //   1111
  //   0111
  //   0000
  //   1011
  //   0000
  //   1000
  //   1111
endmodule
