// Logisim project cpu.circ as structural Verilog: 5 circuits, main circuit 5Up
module main (
  input  Clear_PC
);

  wire clock_1_out, comparator_1_lt, counter_1_carry, demultiplexer_1_out0, demultiplexer_1_out1,
       demultiplexer_1_out2, demultiplexer_1_out3, demultiplexer_1_out4, demultiplexer_1_out5,
       demultiplexer_1_out6, halt_out, nand_1_out, not_1_out, not_2_out, not_3_out, Reset, TClock, xor_1_out;
  wire [2:0] D, rom_1_data;
  wire [3:0] multiplexer_4_out;
  wire [4:0] counter_1_q, MSB, n5up_1_p3;
  wire [6:0] adder_1_out, LSB;
  wire [8:0] alu_1_out_4, multiplexer_1_out, multiplexer_2_out, multiplexer_3_out, R0, R1, R2, R3, R4, R5, R6;
  wire [31:0] ram_1_data;

  not not_1 (not_1_out, xor_1_out);
  // Probe on n5up_1_p3
  // _5Up 5up_1: pin names not known; wires that end beside it: not_1_out, Clear_PC, n5up_1_p3
  xor xor_1 (xor_1_out, TClock, halt_out);
  RAM #(.addrWidth(5), .dataWidth(32)) ram_1 (
    .addr(n5up_1_p3), .data({ram_1_data[31:12], D, ram_1_data[8:0]}));  // open: sel, clk, ld, clr
  and halt (halt_out, ram_1_data[18], ram_1_data[19], ram_1_data[20], ram_1_data[21]);
  // Probe on R0
  not not_2 (not_2_out, ram_1_data[20]);
  nand nand_1 (nand_1_out, ram_1_data[18], ram_1_data[19], not_2_out, ram_1_data[21]);
  // Probe on R1
  Multiplexer #(.select(3), .width(9)) multiplexer_1 (
    .in0(R0), .in1(R1), .in2(R2), .in3(R3), .in4(R4), .in5(R5), .in6(R6), .out(multiplexer_1_out),
    .sel(ram_1_data[17:15]));  // open: in7, en
  // Probe on R2
  ALU alu_1 (.A(multiplexer_1_out), .out_4(alu_1_out_4), .B(multiplexer_3_out), .OPCODE(ram_1_data[21:18]));
  // Probe on R3
  Multiplexer #(.select(3), .width(9)) multiplexer_2 (
    .in0(R0), .in1(R1), .in2(R2), .in3(R3), .in4(R4), .in5(R5), .in6(R6), .out(multiplexer_2_out),
    .sel(ram_1_data[14:12]));  // open: in7, en
  Multiplexer #(.width(9)) multiplexer_3 (
    .in0(multiplexer_2_out), .in1(ram_1_data[8:0]), .out(multiplexer_3_out), .sel(ram_1_data[21]));  // open: en
  // Probe on R4
  Demultiplexer #(.select(3)) demultiplexer_1 (
    .out0(demultiplexer_1_out0), .out1(demultiplexer_1_out1), .out2(demultiplexer_1_out2),
    .out3(demultiplexer_1_out3), .out4(demultiplexer_1_out4), .out5(demultiplexer_1_out5),
    .out6(demultiplexer_1_out6), .in(TClock), .sel(D), .en(nand_1_out));  // open: out7
  TTY #(.rows(33), .cols(1)) tty_1 (.data({2'b10, MSB}), .clk(TClock), .clr(Reset));  // open: we
  // Probe on R5
  _9REG u_9reg_1 (.in_1(alu_1_out_4), .out_3(R0), .CLK(demultiplexer_1_out0));
  _9REG u_9reg_2 (.in_1(alu_1_out_4), .out_3(R1), .CLK(demultiplexer_1_out1));
  _9REG u_9reg_3 (.in_1(alu_1_out_4), .out_3(R2), .CLK(demultiplexer_1_out2));
  _9REG u_9reg_4 (.in_1(alu_1_out_4), .out_3(R3), .CLK(demultiplexer_1_out3));
  _9REG u_9reg_5 (.in_1(alu_1_out_4), .out_3(R4), .CLK(demultiplexer_1_out4));
  _9REG u_9reg_6 (.in_1(alu_1_out_4), .out_3(R5), .CLK(demultiplexer_1_out5));
  TTY #(.rows(33), .cols(1)) tty_2 (.data(LSB), .clk(TClock), .clr(Reset));  // open: we
  // Probe on R6
  _9REG u_9reg_7 (.in_1(alu_1_out_4), .out_3(R6), .CLK(demultiplexer_1_out6));
  // Probe on alu_1_out_4
  Button u_Reset (.out(Reset));
  Counter #(.width(5), .max('h1f), .ongoal("stay")) counter_1 (
    .Q(counter_1_q), .carry(counter_1_carry), .clk(TClock), .clr(Reset));  // open: load, D, count
  Multiplexer #(.select(3), .width(9), .disabled(0), .enable("false")) multiplexer_4 (
    .in0(R0), .in1(R1), .in2(R2), .in3(R3), .in4(R4), .in5(R5), .in6(R6), .out({MSB, multiplexer_4_out}),
    .sel(rom_1_data));  // open: in7
  not not_3 (not_3_out, counter_1_carry);
  Clock clock_1 (.out(clock_1_out));
  and and_1 (TClock, not_3_out, clock_1_out);
  ROM #(.addrWidth(5), .dataWidth(3)) rom_1 (.addr(counter_1_q), .data(rom_1_data));  // open: sel
  // Probe on {3'b011, multiplexer_4_out}
  // Probe on {2'b10, MSB}
  Comparator #(.width(7)) comparator_1 (
    .a(7'b0111001), .b({3'b011, multiplexer_4_out}), .lt(comparator_1_lt));  // open: gt, eq
  // Probe on LSB
  Multiplexer #(.width(7), .disabled(0), .enable("false")) multiplexer_5 (
    .in0({3'b011, multiplexer_4_out}), .in1(adder_1_out), .out(LSB), .sel(comparator_1_lt));
  Adder #(.width(7)) adder_1 (.a({3'b011, multiplexer_4_out}), .b(7'b0000111), .out(adder_1_out));  // open: cin, cout

  // Notes on the sheet:
  //   WAI SHING YUNG
  //   996936848
  //   @0
  //   JA
  //   E5
  //   @0
  //   0F
  //   U5
  //   OF
  //   E5
  //   E5
  //   U4
  //   E5
  //   E5
  //   U4
  //   _F
  //   _F
  //   _F
  //   AF
  //   AF
  //   AF
  //   @0
  //   AE
  //   AE
  //   AE
  //   _E
  //   OF
  //   ^0
  //   J9
  //   P1
  //   R0
  //   R0
  //   _F
  //   contents of rom_1 (hex, n*v repeats v):
  //   0 0 1 2 3 4 5 6 6 2 3 4 5 6 6 0 1 2 3 4 5 6 6 2 3 4 5 6 6 6
endmodule

module _5Up (
  input  in_1,
  input  CLK,
  output [4:0] out_3
);

  wire d_ff_1_qn, d_ff_2_qn, d_ff_3_qn, d_ff_4_qn, d_ff_5_qn;

  D_Flip_Flop d_ff_1 (.clk(CLK), .D(d_ff_1_qn), .Q(out_3[0]), .Qn(d_ff_1_qn), .reset(in_1));  // open: preset, en
  D_Flip_Flop d_ff_2 (.clk(d_ff_1_qn), .D(d_ff_2_qn), .Q(out_3[1]), .Qn(d_ff_2_qn), .reset(in_1));  // open: preset, en
  D_Flip_Flop d_ff_3 (.clk(d_ff_2_qn), .D(d_ff_3_qn), .Q(out_3[2]), .Qn(d_ff_3_qn), .reset(in_1));  // open: preset, en
  D_Flip_Flop d_ff_4 (.clk(d_ff_3_qn), .D(d_ff_4_qn), .Q(out_3[3]), .Qn(d_ff_4_qn), .reset(in_1));  // open: preset, en
  D_Flip_Flop d_ff_5 (.clk(d_ff_4_qn), .D(d_ff_5_qn), .Q(out_3[4]), .Qn(d_ff_5_qn), .reset(in_1));  // open: preset, en
endmodule

module ALU (
  input  [8:0] A,
  input  [8:0] B,
  input  [3:0] OPCODE,
  output [8:0] out_4
);

  wire and_10_out, and_11_out, and_12_out, and_13_out, and_14_out, and_15_out, and_16_out, and_17_out,
       C1_out, C2_out, C3_out, C4_out, C5_out, C6_out, C7_2_out, C7_out, G0_out, G1_out, G2_out, G3_out,
       G4_out, G5_out, G6_out, G7_out, multiplexer_2_out, not_1_out, P0_out, P1_out, P2_out, P3_out, P4_out,
       P5_out, P6_out, P7_out, submux;
  wire [0:0] SRLA;
  wire [7:0] SRL;
  wire [8:0] ADD, ADDA, ADDB, AND, ANDA, ANDB, demultiplexer_1_out3, demultiplexer_1_out7,
       demultiplexer_1_out8, demultiplexer_1_out9, demultiplexer_2_out3, demultiplexer_2_out7,
       demultiplexer_2_out8, demultiplexer_2_out9, HALT, MOV, MOVB, MOVIA, MOVIB, multiplexer_3_out, NOP,
       NOPA, NOPB, NOT, not_2_out, NOTA, NOTB, OR, ORA, ORB, SLLB, SRLB;
  wire [8:1] SLL;
  wire [8:8] SLLA;

  Demultiplexer #(.select(4), .width(9)) demultiplexer_1 (
    .out0(ANDA), .out1(ORA), .out2(NOTA), .out3(demultiplexer_1_out3), .out4(MOV), .out5({SLLA[8], SLL}),
    .out6({SRL, SRLA[0]}), .out7(demultiplexer_1_out7), .out8(demultiplexer_1_out8),
    .out9(demultiplexer_1_out9), .out10(MOVIA), .out11(NOPA), .out15(HALT), .in(A), .sel(OPCODE));  // open: out12, out13, out14, en
  Demultiplexer #(.select(4), .width(9)) demultiplexer_2 (
    .out0(ANDB), .out1(ORB), .out2(NOTB), .out3(demultiplexer_2_out3), .out4(MOVB), .out5(SLLB), .out6(SRLB),
    .out7(demultiplexer_2_out7), .out8(demultiplexer_2_out8), .out9(demultiplexer_2_out9), .out10(MOVIB),
    .out11(NOPB), .out15(HALT), .in(B), .sel(OPCODE));  // open: out12, out13, out14, en
  Multiplexer #(.select(4), .width(9)) multiplexer_1 (
    .in0(AND), .in1(OR), .in2(NOT), .in3(ADD), .in4(MOV), .in5({SLL, 1'b0}), .in6({1'b0, SRL}), .in7(ADD),
    .in8(ADD), .in9(ADD), .in10(B), .in11(NOP), .in15(HALT), .out(out_4), .sel(OPCODE));  // open: in12, in13, in14, en
  assign ADDA = demultiplexer_1_out3 | demultiplexer_1_out7 | demultiplexer_1_out8 | demultiplexer_1_out9;  // OR_Gate or_1, 9 bits wide
  or or_2 (submux, demultiplexer_2_out7[0], demultiplexer_2_out7[1], demultiplexer_2_out7[2], demultiplexer_2_out7[3], demultiplexer_2_out7[4], demultiplexer_2_out7[5], demultiplexer_2_out7[6], demultiplexer_2_out7[7], demultiplexer_2_out7[8], demultiplexer_2_out9[0], demultiplexer_2_out9[1], demultiplexer_2_out9[2], demultiplexer_2_out9[3], demultiplexer_2_out9[4], demultiplexer_2_out9[5], demultiplexer_2_out9[6], demultiplexer_2_out9[7], demultiplexer_2_out9[8]);
  assign ADDB = demultiplexer_2_out8 | demultiplexer_2_out9 | demultiplexer_2_out3 | demultiplexer_2_out7;  // OR_Gate or_3, 9 bits wide
  and and_1 (AND[8], ANDB[8], ANDA[8]);
  and and_2 (AND[7], ANDB[7], ANDA[7]);
  and and_3 (AND[6], ANDB[6], ANDA[6]);
  and and_4 (AND[3], ANDB[3], ANDA[3]);
  and and_5 (AND[5], ANDB[5], ANDA[5]);
  and and_6 (AND[4], ANDB[4], ANDA[4]);
  and and_7 (AND[1], ANDB[1], ANDA[1]);
  and and_8 (AND[2], ANDB[2], ANDA[2]);
  and and_9 (AND[0], ANDB[0], ANDA[0]);
  or C7 (C7_out, and_10_out, G7_out);
  and and_10 (and_10_out, C7_2_out, P7_out);
  or or_4 (OR[7], ORB[7], ORA[7]);
  or or_5 (OR[8], ORB[8], ORA[8]);
  or or_6 (OR[6], ORB[6], ORA[6]);
  or C6 (C6_out, and_12_out, G5_out);
  or C7_2 (C7_2_out, and_11_out, G6_out);
  and and_11 (and_11_out, C6_out, P6_out);
  and and_12 (and_12_out, C5_out, P5_out);
  Multiplexer multiplexer_2 (.in0(1'b0), .in1(not_1_out), .out(multiplexer_2_out), .sel(submux));  // open: en
  not not_1 (not_1_out, 1'b0);
  // OR_Gate P8 has open pins: in0=ADDA[8], in1=multiplexer_3_out[8], out=open
  or or_7 (OR[5], ORB[5], ORA[5]);
  or or_8 (OR[3], ORB[3], ORA[3]);
  or or_9 (OR[4], ORB[4], ORA[4]);
  or C5 (C5_out, and_13_out, G4_out);
  and and_13 (and_13_out, C4_out, P4_out);
  or P7 (P7_out, ADDA[7], multiplexer_3_out[7]);
  or P6 (P6_out, ADDA[6], multiplexer_3_out[6]);
  or or_10 (OR[1], ORB[1], ORA[1]);
  or or_11 (OR[2], ORB[2], ORA[2]);
  or C4 (C4_out, and_15_out, G3_out);
  or C3 (C3_out, and_14_out, G2_out);
  and and_14 (and_14_out, C2_out, P2_out);
  and and_15 (and_15_out, C3_out, P3_out);
  or P4 (P4_out, ADDA[4], multiplexer_3_out[4]);
  or P5 (P5_out, ADDA[5], multiplexer_3_out[5]);
  or P3 (P3_out, ADDA[3], multiplexer_3_out[3]);
  or or_12 (OR[0], ORB[0], ORA[0]);
  or C2 (C2_out, and_17_out, G1_out);
  or C1 (C1_out, and_16_out, G0_out);
  and and_16 (and_16_out, multiplexer_2_out, P0_out);
  and and_17 (and_17_out, C1_out, P1_out);
  or P2 (P2_out, ADDA[2], multiplexer_3_out[2]);
  or P0 (P0_out, ADDA[0], multiplexer_3_out[0]);
  or P1 (P1_out, ADDA[1], multiplexer_3_out[1]);
  and G0 (G0_out, multiplexer_3_out[0], ADDA[0]);
  and G1 (G1_out, multiplexer_3_out[1], ADDA[1]);
  and G2 (G2_out, multiplexer_3_out[2], ADDA[2]);
  and G3 (G3_out, multiplexer_3_out[3], ADDA[3]);
  and G4 (G4_out, multiplexer_3_out[4], ADDA[4]);
  and G5 (G5_out, multiplexer_3_out[5], ADDA[5]);
  and G6 (G6_out, multiplexer_3_out[6], ADDA[6]);
  and G7 (G7_out, multiplexer_3_out[7], ADDA[7]);
  // AND_Gate G8 has open pins: in0=multiplexer_3_out[8], in1=ADDA[8], out=open
  assign not_2_out = ~ADDB;  // NOT_Gate not_2, 9 bits wide
  assign NOT = ~NOTA;  // NOT_Gate not_3, 9 bits wide
  Multiplexer #(.width(9)) multiplexer_3 (
    .in0(ADDB), .in1(not_2_out), .out(multiplexer_3_out), .sel(submux));  // open: en
  BADDR baddr_1 (.in_1(ADDA[0]), .in_2(multiplexer_3_out[0]), .in_3(multiplexer_2_out), .out_4(ADD[0]));
  BADDR baddr_2 (.in_1(ADDA[1]), .in_2(multiplexer_3_out[1]), .in_3(C1_out), .out_4(ADD[1]));
  BADDR baddr_3 (.in_1(ADDA[2]), .in_2(multiplexer_3_out[2]), .in_3(C2_out), .out_4(ADD[2]));
  BADDR baddr_4 (.in_1(ADDA[3]), .in_2(multiplexer_3_out[3]), .in_3(C3_out), .out_4(ADD[3]));
  BADDR baddr_5 (.in_1(ADDA[4]), .in_2(multiplexer_3_out[4]), .in_3(C4_out), .out_4(ADD[4]));
  BADDR baddr_6 (.in_1(ADDA[5]), .in_2(multiplexer_3_out[5]), .in_3(C5_out), .out_4(ADD[5]));
  BADDR baddr_7 (.in_1(ADDA[6]), .in_2(multiplexer_3_out[6]), .in_3(C6_out), .out_4(ADD[6]));
  BADDR baddr_8 (.in_1(ADDA[7]), .in_2(multiplexer_3_out[7]), .in_3(C7_2_out), .out_4(ADD[7]));
  BADDR baddr_9 (.in_1(ADDA[8]), .in_2(multiplexer_3_out[8]), .in_3(C7_out), .out_4(ADD[8]));

  // Other names for the same wires on the sheet: MOVA[8:0] = MOV; MOVI[8:0] = B; SLLA[7:0] = SLL; SRLA[8:1] = SRL;
  //   ADDI[8:0] = ADD; SUB[8:0] = ADD; SUBI[8:0] = ADD

  // Notes on the sheet:
  //   anti-claustrophobia
  //   anti-claustrophobia
endmodule

module BADDR (
  input  in_1,
  input  in_2,
  input  in_3,
  output out_4
);

  wire xor_1_out;

  xor xor_1 (xor_1_out, in_1, in_2);
  xor xor_2 (out_4, xor_1_out, in_3);
endmodule

module _9REG (
  input  [8:0] in_1,
  input  CLK,
  output [8:0] out_3
);

  D_Flip_Flop d_ff_1 (.clk(CLK), .D(in_1[5]), .Q(out_3[5]));  // open: Qn, preset, en, reset
  D_Flip_Flop d_ff_2 (.clk(CLK), .D(in_1[6]), .Q(out_3[6]));  // open: Qn, preset, en, reset
  D_Flip_Flop d_ff_3 (.clk(CLK), .D(in_1[7]), .Q(out_3[7]));  // open: Qn, preset, en, reset
  D_Flip_Flop d_ff_4 (.clk(CLK), .D(in_1[8]), .Q(out_3[8]));  // open: Qn, preset, en, reset
  D_Flip_Flop d_ff_5 (.clk(CLK), .D(in_1[0]), .Q(out_3[0]));  // open: Qn, preset, en, reset
  D_Flip_Flop d_ff_6 (.clk(CLK), .D(in_1[1]), .Q(out_3[1]));  // open: Qn, preset, en, reset
  D_Flip_Flop d_ff_7 (.clk(CLK), .D(in_1[2]), .Q(out_3[2]));  // open: Qn, preset, en, reset
  D_Flip_Flop d_ff_8 (.clk(CLK), .D(in_1[3]), .Q(out_3[3]));  // open: Qn, preset, en, reset
  D_Flip_Flop d_ff_9 (.clk(CLK), .D(in_1[4]), .Q(out_3[4]));  // open: Qn, preset, en, reset
endmodule
