// Logisim project alutest.circ as structural Verilog: 1 circuit, main circuit main
module main (
);

  wire A0, A1, A2, Ad0, Ad1, Ad2, Ad3, and_1_out, B0, B1, B2, C0, C1, C2, CIN, clock_1_out, not_1_out,
       Reset_out, S0, S1, stop;
  wire [11:3] rom_1_data;

  Clock clock_1 (.out(clock_1_out));
  not not_1 (not_1_out, stop);
  // Probe on CIN
  // Probe on {C2, C1, C0}
  and and_1 (and_1_out, clock_1_out, not_1_out);
  // Probe on {S1, S0}
  TTY #(.rows(1), .cols(10)) tty_1 (.data({4'b0110, C2, C1, C0}), .clk(and_1_out), .clr(Reset_out));  // open: we
  Counter #(.width(4), .max('ha), .ongoal("stay")) counter_1 (
    .Q({Ad3, Ad2, Ad1, Ad0}), .carry(stop), .clk(and_1_out), .clr(Reset_out));  // open: load, D, count
  // Probe on {rom_1_data[11], CIN, S1, S0, rom_1_data[7], B2, B1, B0, rom_1_data[3], A2, A1, A0}
  ROM #(.addrWidth(4), .dataWidth(12)) rom_1 (
    .addr({Ad3, Ad2, Ad1, Ad0}),
    .data({rom_1_data[11], CIN, S1, S0, rom_1_data[7], B2, B1, B0, rom_1_data[3], A2, A1, A0}));  // open: sel
  // Probe on {B2, B1, B0}
  // Probe on {A2, A1, A0}
  Button Reset (.out(Reset_out));

  // Notes on the sheet:
  //   adds 48 to make printable
  //   5 & 3, 6 & 2, 5 | 3, 6 | 2, ~5, ~2, 7 + 7 + 0, 5 + 3 + 0, 6 + 4 + 1, 3 + 2 + 1
  //   1276256036
  //   contents of rom_1 (hex, n*v repeats v):
  //   53 62 153 162 205 202 377 353 764 723
endmodule
