// Logisim project adder.circ as structural Verilog: 1 circuit, main circuit main
module main (
);

  wire A, and_1_out, and_2_out, B, C, carry, clock_1_out, go, Reset_out, sum, t_ff_1_q, t_ff_2_q, t_ff_4_q,
       xor_1_out;

  xor xor_1 (xor_1_out, A, B);
  and and_1 (and_1_out, B, A);
  and and_2 (and_2_out, xor_1_out, C);
  xor xor_2 (sum, xor_1_out, C);
  or or_1 (carry, and_2_out, and_1_out);
  // Probe on {A, B, C}
  Clock clock_1 (.out(clock_1_out));
  T_Flip_Flop t_ff_1 (.clk(clock_1_out), .T(1'b1), .Q(t_ff_1_q), .Qn(C), .preset(Reset_out), .en(go));  // open: reset
  T_Flip_Flop t_ff_2 (.clk(t_ff_1_q), .T(1'b1), .Q(t_ff_2_q), .Qn(B), .preset(Reset_out));  // open: reset, en
  TTY #(.rows(1), .cols(8)) tty_1 (.data({5'b01100, carry, sum}), .clk(clock_1_out), .we(go), .clr(Reset_out));
  T_Flip_Flop t_ff_3 (.clk(t_ff_4_q), .T(1'b1), .Q(go), .preset(Reset_out));  // open: Qn, reset, en
  T_Flip_Flop t_ff_4 (.clk(t_ff_2_q), .T(1'b1), .Q(t_ff_4_q), .Qn(A), .preset(Reset_out));  // open: reset, en
  Button Reset (.out(Reset_out));

  // Notes on the sheet:
  //   Wai Shing Yung
  //   996936848
  //   01121223
endmodule
