// Logisim project bcd.circ as structural Verilog: 1 circuit, main circuit main
module main (
);

  wire a, and_1_out, b, c, clock_1_out, d, e, f, g, not_1_out, not_2_out, not_3_out, not_4_out, not_5_out,
       nw1_nw0_out, nw2_nw0_out, nw2w1_out, Reset_out, stop, w0, w1, W1_nw0_out, w1w0_out, w2, w2_nw0_out,
       w2_nw1_out, W2_nW1W0_out, w2w0_out, w3;

  not not_1 (not_1_out, w0);
  not not_2 (not_2_out, w1);
  not not_3 (not_3_out, w2);
  not not_4 (not_4_out, w3);
  and w1w0 (w1w0_out, w0, w1);
  and W1_nw0 (W1_nw0_out, not_1_out, w1, w1);
  and nw1_nw0 (nw1_nw0_out, not_1_out, not_2_out, not_2_out);
  and w2w0 (w2w0_out, w0, w2);
  and w2_nw0 (w2_nw0_out, not_1_out, w2);
  and nw2_nw0 (nw2_nw0_out, not_1_out, not_1_out, not_3_out);
  and W2_nW1W0 (W2_nW1W0_out, w0, not_2_out, w2);
  and w2_nw1 (w2_nw1_out, not_2_out, w2);
  and nw2w1 (nw2w1_out, w1, not_3_out);
  or or_1 (a, nw2_nw0_out, w1, w2w0_out, w3);
  or or_2 (b, not_3_out, w1w0_out, nw1_nw0_out, w3);
  or or_3 (d, W1_nw0_out, nw2_nw0_out, W2_nW1W0_out, w3, nw2w1_out);
  or or_4 (c, w0, not_2_out, w2);
  or or_5 (e, W1_nw0_out, nw2_nw0_out);
  or or_6 (f, w3, w2_nw1_out, w2_nw0_out, nw1_nw0_out);
  or or_7 (g, w3, W1_nw0_out, w2_nw1_out, nw2w1_out);
  _7_Segment_Display u_7_segment_display_1 (.g(g), .f(f), .a(a), .b(b), .e(e), .d(d), .c(c));  // open: dp
  Clock clock_1 (.out(clock_1_out));
  // Probe on {w3, w2, w1, w0}
  and and_1 (and_1_out, clock_1_out, not_5_out);
  not not_5 (not_5_out, stop);
  TTY #(.rows(10), .cols(1)) tty_1 (.data({3'b100, d, c, b, a}), .clk(and_1_out), .clr(Reset_out));  // open: we
  Counter #(.width(4), .max('h9), .ongoal("stay")) counter_1 (
    .Q({w3, w2, w1, w0}), .carry(stop), .clk(and_1_out), .clr(Reset_out));  // open: load, D, count
  TTY #(.rows(10), .cols(1)) tty_2 (.data({4'b0110, g, f, e}), .clk(and_1_out), .clr(Reset_out));  // open: we
  Button Reset (.out(Reset_out));

  // Notes on the sheet:
  //   Wai Shing Yung
  //   996936848
  //   O
  //   F
  //   K
  //   O
  //   F
  //   M
  //   M
  //   G
  //   O
  //   3
  //   0
  //   5
  //   4
  //   6
  //   6
  //   7
  //   0
  //   7
endmodule
