// Logisim project bits.circ as structural Verilog: 1 circuit, main circuit main
module main (
  input  in_1
);

  wire _1_s, _2_s, _4_s, clock, go, Reset_out, t_ff_1_q, t_ff_2_q, t_ff_3_q, t_ff_4_q, t_ff_5_q, t_ff_6_q,
       x1, x2, x3, x4, x5, x6;
  wire [3:3] bitadder_1_out;

  // Probe on {x1, x2, x3, x4, x5, x6}
  Clock clock_1 (.out(clock));
  BitAdder bitadder_1 (.in0({{2{in_1}}, x1, x2, x3, x4, x5, x6}), .out({bitadder_1_out[3], _4_s, _2_s, _1_s}));
  T_Flip_Flop t_ff_1 (.clk(t_ff_2_q), .T(1'b1), .Q(t_ff_1_q), .Qn(x5), .preset(Reset_out));  // open: reset, en
  T_Flip_Flop t_ff_2 (.clk(clock), .T(1'b1), .Q(t_ff_2_q), .Qn(x6), .preset(Reset_out), .en(go));  // open: reset
  // Probe on {bitadder_1_out[3], _4_s, _2_s, _1_s}
  TTY #(.rows(1), .cols(64)) tty_1 (.data({4'b0110, _4_s, _2_s, _1_s}), .clk(clock), .we(go), .clr(Reset_out));
  T_Flip_Flop t_ff_3 (.clk(t_ff_1_q), .T(1'b1), .Q(t_ff_3_q), .Qn(x4), .preset(Reset_out));  // open: reset, en
  T_Flip_Flop t_ff_4 (.clk(t_ff_3_q), .T(1'b1), .Q(t_ff_4_q), .Qn(x3), .preset(Reset_out));  // open: reset, en
  T_Flip_Flop t_ff_5 (.clk(t_ff_4_q), .T(1'b1), .Q(t_ff_5_q), .Qn(x2), .preset(Reset_out));  // open: reset, en
  T_Flip_Flop t_ff_6 (.clk(t_ff_5_q), .T(1'b1), .Q(t_ff_6_q), .Qn(x1), .preset(Reset_out));  // open: reset, en
  T_Flip_Flop t_ff_7 (.clk(t_ff_6_q), .T(1'b1), .Q(go), .preset(Reset_out));  // open: Qn, reset, en
  Button Reset (.out(Reset_out));

  // Notes on the sheet:
  //   Wai Shing Yung
  //   996936848
  //   Press Reset button, then Ctrl-k or Ctrl-t
  //   0112122312232334122323342334344512232334233434452334344534454556
endmodule
