// Logisim project sectest.circ as structural Verilog: 1 circuit, main circuit main
module main (
);

  wire A0, A1, A2, C0, C1, C2, C3, clock_1_out, D0, D1, D2, D3, D4, D5, D6, D7, go, P0, P1, P2, Reset_out,
       t_ff_1_q, t_ff_2_q, t_ff_3_q, t_ff_4_q, t_ff_5_q, t_ff_6_q, Z0, Z1, Z2, Z3, Z4, Z5, Z6, Z7;
  wire [0:0] multiplexer_1_out;

  Clock clock_1 (.out(clock_1_out));
  T_Flip_Flop t_ff_1 (.clk(clock_1_out), .T(1'b1), .Q(t_ff_1_q), .Qn(P0), .preset(Reset_out), .en(go));  // open: reset
  Multiplexer #(.select(3), .disabled(0), .enable("false")) multiplexer_1 (
    .in0(Z7), .in1(Z6), .in2(Z5), .in3(Z4), .in4(Z3), .in5(Z2), .in6(Z1), .in7(Z0),
    .out(multiplexer_1_out[0]), .sel({P2, P1, P0}));
  T_Flip_Flop t_ff_2 (.clk(t_ff_1_q), .T(1'b1), .Q(t_ff_2_q), .Qn(P1), .preset(Reset_out));  // open: reset, en
  T_Flip_Flop t_ff_3 (.clk(t_ff_2_q), .T(1'b1), .Q(t_ff_3_q), .Qn(P2), .preset(Reset_out));  // open: reset, en
  ROM #(.addrWidth(3), .dataWidth(12)) rom_1 (
    .addr({A2, A1, A0}), .data({D7, D6, D5, D4, C3, D3, D2, D1, C2, D0, C1, C0}));  // open: sel
  TTY #(.cols(8)) tty_1 (.data({6'b011000, multiplexer_1_out[0]}), .clk(clock_1_out), .we(go), .clr(Reset_out));
  T_Flip_Flop t_ff_4 (.clk(t_ff_3_q), .T(1'b1), .Q(t_ff_4_q), .Qn(A0), .preset(Reset_out));  // open: reset, en
  // Probe on {D7, D6, D5, D4, C3, D3, D2, D1, C2, D0, C1, C0}
  T_Flip_Flop t_ff_5 (.clk(t_ff_4_q), .T(1'b1), .Q(t_ff_5_q), .Qn(A1), .preset(Reset_out));  // open: reset, en
  T_Flip_Flop t_ff_6 (.clk(t_ff_5_q), .T(1'b1), .Q(t_ff_6_q), .Qn(A2), .preset(Reset_out));  // open: reset, en
  Button Reset (.out(Reset_out));
  T_Flip_Flop t_ff_7 (.clk(t_ff_6_q), .T(1'b1), .Q(go), .preset(Reset_out));  // open: Qn, reset, en

  // Notes on the sheet:
  //   contents of rom_1 (hex, n*v repeats v):
  //   d7 788 a75 a74 275 b75 f75 a77
  //   00101011
  //   01110000
  //   10101111
  //   10101111
  //   10101111
  //   10101111
  //   11111111
  //   10101111
endmodule
