// Logisim project vending.circ as structural Verilog: 1 circuit, main circuit main
module main (
);

  wire _4_Counter_carry, A, and_1_out, and_2_out, and_3_out, and_4_out, and_5_out, and_6_out, and_7_out,
       and_8_out, and_9_out, and_10_out, and_11_out, and_12_out, and_13_out, and_14_out, and_15_out,
       and_16_out, and_17_out, and_18_out, and_19_out, and_20_out, and_21_out, and_22_out, and_23_out, B, C,
       CLK, clock_1_out, clock_2_out, go, not_1_out, not_2_out, not_3_out, not_4_out, not_5_out, not_6_out,
       not_7_out, not_8_out, not_9_out, not_10_out, not_11_out, not_12_out, or_1_out, or_2_out, or_3_out,
       Reset_out, x1, x2, x3, z1, z2, z3;
  wire [4:0] _4_Counter_q;

  not not_1 (not_1_out, A);
  not not_2 (not_2_out, B);
  not not_3 (not_3_out, C);
  not not_4 (not_4_out, x1);
  not not_5 (not_5_out, x2);
  not not_6 (not_6_out, x3);
  and and_1 (and_1_out, A, C);
  and and_2 (and_2_out, A, x1);
  and and_3 (and_3_out, A, x2);
  and and_4 (and_4_out, not_2_out, not_3_out, x1);
  and and_5 (and_5_out, B, x2);
  and and_6 (and_6_out, B, C, not_4_out);
  and and_7 (and_7_out, not_1_out, x2);
  or or_1 (or_1_out, and_7_out, and_8_out, and_9_out);
  and and_8 (and_8_out, not_1_out, C, not_4_out);
  and and_9 (and_9_out, B, not_5_out, not_6_out);
  and and_10 (and_10_out, not_1_out, not_2_out, not_5_out);
  and and_11 (and_11_out, B, x3);
  and and_12 (and_12_out, B, C, not_5_out);
  and and_13 (and_13_out, A, x3);
  and and_14 (and_14_out, A, C);
  Clock clock_1 (.out(clock_1_out));
  or or_2 (or_2_out, and_1_out, and_2_out, and_3_out, and_4_out, and_5_out, and_6_out);
  or or_3 (or_3_out, and_10_out, and_11_out, and_12_out, and_13_out, and_14_out);
  not not_7 (not_7_out, A);
  T_Flip_Flop t_ff_1 (.clk(clock_1_out), .T(or_2_out), .Q(A));  // open: Qn, preset, reset, en
  T_Flip_Flop t_ff_2 (.clk(clock_1_out), .T(or_1_out), .Q(B));  // open: Qn, preset, reset, en
  T_Flip_Flop t_ff_3 (.clk(clock_1_out), .T(or_3_out), .Q(C));  // open: Qn, preset, reset, en
  not not_8 (not_8_out, C);
  not not_9 (not_9_out, B);
  not not_10 (not_10_out, x2);
  not not_11 (not_11_out, x1);
  not not_12 (not_12_out, x3);
  and and_15 (and_15_out, not_7_out, not_9_out, C, x1);
  and and_16 (and_16_out, A, not_9_out, C, not_11_out);
  and and_17 (and_17_out, A, not_12_out);
  and and_18 (and_18_out, B, x1, not_10_out);
  and and_19 (and_19_out, A, x1);
  and and_20 (and_20_out, B, C, x1);
  and and_21 (and_21_out, A, x1);
  and and_22 (and_22_out, A, C, x2);
  and and_23 (and_23_out, B, not_8_out, x1);
  TTY #(.rows(1), .cols(33)) tty_1 (.data({4'b0110, z1, z2, z3}), .clk(CLK), .we(go), .clr(Reset_out));
  or or_4 (z2, and_19_out, and_20_out);
  or or_5 (z3, and_21_out, and_22_out, and_23_out);
  or or_6 (z1, and_15_out, and_16_out, and_17_out, and_18_out);
  Button Reset (.out(Reset_out));
  // Probe on _4_Counter_q
  Counter #(.width(5), .max('h1f)) _4_Counter (
    .Q(_4_Counter_q), .carry(_4_Counter_carry), .clk(CLK), .clr(Reset_out));  // open: load, D, count
  and and_24 (CLK, clock_2_out, go);
  Clock clock_2 (.out(clock_2_out));
  not not_13 (go, _4_Counter_carry);
  ROM #(.addrWidth(5), .dataWidth(3)) rom_1 (.addr(_4_Counter_q), .data({x1, x2, x3}));  // open: sel
  // Probe on x3
  // Probe on x2
  // Probe on x1

  // Notes on the sheet:
  //   996936848
  //   Wai Shing Yung
  //   26 Gates
  //   0400000500040060500700605004000
  //   contents of rom_1 (hex, n*v repeats v):
  //   4 6*1 2 1 1 2 2 2 1 4 2 4 2 2 4 1 2 4 2 4 2 2 2 1 1 1 2
endmodule
